# Fritzing sketch sound_amp_for_surrogate_hat (saved by Fritzing 0.9.3b)
breadboards: 1

parts:
  U1 = Stereo 3.7W Class D Amplifier [part_number="Adafruit carrier" package=14-tdfn]
  male_1/8"_jack_to_sound_source = 2.5mm Audio Jack [package=stereojack2.5mm_stereojack2.5mm]
  battery = Battery block 9V
  U2 = Voltage Regulator - 5V [package="TO220 [THT]"]
  SP1 = SPEAKER [part_number="bone conduction transducers, 8Ω each" package=pcb_mount_speaker]
  SP2 = SPEAKER [package=pcb_mount_speaker]

nets:
  GND: U1.GND, battery.-, U2.GND
  N1: U1.INL+, U1.INR+, male_1/8"_jack_to_sound_source.SLEEVE
  N2: U1.INL-, U1.INR-, male_1/8"_jack_to_sound_source.RIGHT
  N3: U1.OUTR-, SP2.-
  N4: U1.OUTR+, SP2.+
  N5: U1.VDD, U2.output_voltage
  N6: U1.OUTL+, SP1.+
  N7: U1.OUTL-, SP1.-
  N8: battery.+, U2.input_voltage
